# Fritzing sketch 3V3_Linear_Regulator (saved by Fritzing 0.9.4)
breadboards: 1

parts:
  D1 = TLV431 [part_number=TLV451 package="TO-92 [THT]"]
  R1 = Resistor [tolerance=±5% resistance=1.7k package="0805 [SMD]"]
  U1 = LM358 [package=dip08]
  R2 = Resistor [tolerance=±5% resistance=47k package="0805 [SMD]"]
  R3 = Resistor [tolerance=±5% resistance=1.7k package="0805 [SMD]"]
  R4 = Resistor [tolerance=±5% resistance=1.7k package="0805 [SMD]"]
  R7 = Resistor [tolerance=±5% resistance=47k package="0805 [SMD]"]
  Q1 = Basic FET P-Channel [package="DPak [SMD]"]
  R8 = Resistor [tolerance=±5% resistance=270 package="0805 [SMD]"]
  R9 = Resistor [tolerance=±5% resistance=33 package="0805 [SMD]"]
  Q2 = MOSFET-NCHANNEL [package=to220v]
  R10 = Resistor [tolerance=±5% resistance=100 package="0805 [SMD]"]
  C1 = Electrolytic Capacitor [capacitance=10μF package="0605 [SMD, electrolytic]"]
  Part1 = Breadboard Power Supply Board SMD

nets:
  N1: D1.cathode, D1.ref, R1.Pin_0, U1.G$1_-IN
  N2: D1.anode, U1.G$1_V-, R2.Pin_1, R8.Pin_1, Q2.S, C1.-, Part1.GND
  N3: R1.Pin_1, U1.G$1_V+, R7.Pin_1, Q1.source, Part1.VCC
  N4: U1.G$1_OUT, R4.Pin_1
  N5: U1.G$1_+IN, R2.Pin_0, R3.Pin_1
  N6: R3.Pin_0, Q1.drain, R8.Pin_0, R9.Pin_1, C1.+
  N7: R4.Pin_0, R7.Pin_0, Q1.Gate
  N8: R9.Pin_0, Q2.D
  N9: Q2.G, R10.Pin_0

notes:
  REF-ANODE-CATH
  Signal Gen Input (load switching)
  Output Voltage

custom parts:
  TLV431: A TLV431 Precision Shunt Regulator
